# Fritzing sketch Wiring (saved by Fritzing 0.9.3b)

parts:
  DFPlayer_Mini1 = DFPlayer MINI [package="DIP (Dual Inline) [THT]"]
  SPKR1 = Loudspeaker
  R1 = Resistor [tolerance=±5% resistance=1k package=THT]
  R2 = Resistor [tolerance=±5% resistance=1k package=THT]
  Composant2 = Real Time Clock Module - DS1307 RTC Breakout Board
  Composant3 = Arduino Uno (Rev3)
  X1 = USB Connectors [package=usb-a-s-nosilk-female]

nets:
  5V: DFPlayer_Mini1.VCC, Composant2.5V, Composant3.5V, X1.D+
  N1: DFPlayer_Mini1.RX, R1.Pin_1
  N2: DFPlayer_Mini1.TX, R2.Pin_1
  N3: DFPlayer_Mini1.SPK1, SPKR1.pin2
  GND: DFPlayer_Mini1.GND, Composant2.GND, Composant3.GND, X1.D-
  N4: DFPlayer_Mini1.SPK2, SPKR1.pin1
  N5: R1.Pin_0, Composant3.D0/RX
  N6: R2.Pin_0, Composant3.D1/TX
  N7: Composant2.SCL, Composant3.A5/SCL
  N8: Composant2.SDA, Composant3.A4/SDA

notes:
  3W, 5V = 0.6A
  1k Ohm
  enceinte  0.6A, arduino

custom parts:
  DFPlayer MINI: MP3 module by DFRobot.com for playing Music from an SD-Card. Supports WAV and MP3 files.
